// Logisim project 4bitCpu.circ as structural Verilog: 1 circuit, main circuit main
module main (
);

  wire Add, and_1_out, ChangeRomSec, CL, comparator_1_eq, decoder_2_out0, decoder_2_out13, decoder_2_out14,
       decoder_2_out15, GPUclock, JMP, JMPifA0, LDI, LoadColumnBuf, LoadRamBank, LoadRamIntoAFromAdrr, MOV,
       not_2_out, or_1_out, or_2_out, register_1_q, register_2_q, register_3_q, register_4_q, Sub, t_ff_1_q,
       undriven, writeAintoRamAtAdrr, WriteVRam;
  wire [3:0] adder_2_out, Addout, controlled_buffer_1_out, counter_2_q, demultiplexer_1_out0,
       demultiplexer_1_out1, Operand, outA, outB, RamBankAdr, RamOut, RomSec, SubOut, subtractor_1_out,
       VRam_dout;
  wire [7:0] adder_1_out, ColumnBufferOut, counter_1_q, decoder_1_out0, rom_1_data;
  wire [7:4] register_5_q;

  Comparator #(.width(4)) comparator_1 (.a(outA), .b(4'b0000), .eq(comparator_1_eq));  // open: gt, lt
  and and_1 (and_1_out, JMPifA0, comparator_1_eq);
  T_Flip_Flop t_ff_1 (.T(1'b1), .clk(GPUclock), .Q(t_ff_1_q));  // open: Qn, reset, preset
  or or_1 (or_1_out, and_1_out, JMP);
  Clock #(.highDuration(5), .lowDuration(5)) clock_1 (.out(CL));
  not not_1 (LoadColumnBuf, t_ff_1_q);
  Counter counter_1 (
    .clr(1'b0), .load(or_1_out), .up(1'b1), .clk(CL), .D({RomSec, Operand}), .Q(counter_1_q));  // open: count, carry
  Counter #(.max('hf), .width(4)) counter_2 (
    .clr(undriven), .load(WriteVRam), .up(t_ff_1_q), .clk(t_ff_1_q), .D(Operand), .Q(counter_2_q));  // open: count, carry
  Clock clock_2 (.out(GPUclock));
  Register #(.width(1)) register_1 (.D(WriteVRam), .en(1'b1), .clk(GPUclock), .Q(register_1_q));  // open: clr
  Register #(.width(1)) register_2 (.D(Add), .en(1'b1), .clk(CL), .Q(register_2_q));  // open: clr
  Register #(.width(1)) register_3 (.D(Sub), .en(1'b1), .clk(CL), .Q(register_3_q));  // open: clr
  Register #(.width(1)) register_4 (.D(LoadRamIntoAFromAdrr), .en(1'b1), .clk(CL), .Q(register_4_q));  // open: clr
  ROM rom_1 (.addr(counter_1_q), .data(rom_1_data));
  RAM #(.addrWidth(4), .dataWidth(4)) VRam (
    .addr(counter_2_q), .we(register_1_q), .oe(1'b1), .clk(GPUclock), .din(outA), .dout(VRam_dout));
  RAM #(.dataWidth(4)) GeneralRam (
    .addr({Operand, RamBankAdr}), .we(writeAintoRamAtAdrr), .oe(LoadRamIntoAFromAdrr), .clk(CL), .din(outA),
    .dout(RamOut));
  assign controlled_buffer_1_out = register_2_q ? Addout : 4'bz;  // Controlled_Buffer controlled_buffer_1
  assign controlled_buffer_1_out = register_3_q ? SubOut : 4'bz;  // Controlled_Buffer controlled_buffer_2
  assign controlled_buffer_1_out = register_4_q ? RamOut : 4'bz;  // Controlled_Buffer controlled_buffer_3
  assign controlled_buffer_1_out = LDI ? Operand : 4'bz;  // Controlled_Buffer controlled_buffer_4
  or or_2 (or_2_out, register_2_q, register_3_q, register_4_q, LDI);
  Register register_5 (.D(rom_1_data), .en(1'b1), .clk(CL), .Q({register_5_q, Operand}), .clr(1'b0));
  Decoder #(.select(3)) decoder_1 (
    .out0(decoder_1_out0[0]), .out1(decoder_1_out0[1]), .out2(decoder_1_out0[2]), .out3(decoder_1_out0[3]),
    .out4(decoder_1_out0[4]), .out5(decoder_1_out0[5]), .out6(decoder_1_out0[6]), .out7(decoder_1_out0[7]),
    .sel(counter_2_q[3:1]), .en(1'b1));
  not not_2 (not_2_out, counter_2_q[0]);
  Demultiplexer #(.width(4)) demultiplexer_1 (
    .out0(demultiplexer_1_out0), .out1(demultiplexer_1_out1), .in(VRam_dout), .sel(not_2_out));
  Register #(.width(4)) B (.D(outA), .en(MOV), .clk(CL), .Q(outB));  // open: clr
  Register #(.width(4)) A (.D(controlled_buffer_1_out), .en(or_2_out), .clk(CL), .Q(outA));  // open: clr
  Register #(.width(4)) RamBankAdress (.D(Operand), .en(LoadRamBank), .clk(CL), .Q(RamBankAdr));  // open: clr
  Register #(.width(4)) u_RomSec (.D(Operand), .en(ChangeRomSec), .clk(CL), .Q(RomSec));  // open: clr
  // DotMatrix #(.inputtype("select"), .matrixcols(8), .matrixrows(8)) dotmatrix_1: pin names not known; wires that end beside it: ColumnBufferOut, decoder_1_out0
  LED led_1 (.in(MOV));
  LED led_2 (.in(decoder_2_out13));
  LED led_3 (.in(decoder_2_out15));
  Decoder #(.select(4)) decoder_2 (
    .out0(decoder_2_out0), .out1(LDI), .out2(Add), .out3(Sub), .out4(MOV), .out5(MOV), .out6(JMP),
    .out7(JMPifA0), .out8(ChangeRomSec), .out9(LoadRamBank), .out10(writeAintoRamAtAdrr),
    .out11(LoadRamIntoAFromAdrr), .out12(WriteVRam), .out13(decoder_2_out13), .out14(decoder_2_out14),
    .out15(decoder_2_out15), .sel(register_5_q), .en(1'b1));
  Register ColumnBuffer (.D(adder_1_out), .en(LoadColumnBuf), .clk(GPUclock), .Q(ColumnBufferOut));  // open: clr
  Adder adder_1 (
    .a({4'b0000, demultiplexer_1_out0}), .b({demultiplexer_1_out1, 4'b0000}), .out(adder_1_out));  // open: cin, cout
  LED led_4 (.in(decoder_2_out0));
  LED led_5 (.in(decoder_2_out14));
  Adder #(.width(4)) adder_2 (.a(outA), .b(outB), .out(adder_2_out));  // open: cin, cout
  Subtractor #(.width(4)) subtractor_1 (.a(outA), .b(outB), .out(subtractor_1_out));  // open: bin, bout
  Register #(.width(4)) register_6 (.D(adder_2_out), .en(Add), .clk(CL), .Q(Addout));  // open: clr
  Register #(.width(4)) register_7 (.D(subtractor_1_out), .en(Sub), .clk(CL), .Q(SubOut));  // open: clr

  // Notes on the sheet:
  //   contents of rom_1 (hex, n*v repeats v):
  //   13 c0 19 c2 0 0 a0 10 0 b0 0 20 0 a0 0 67
  //   Opcode
endmodule
